// Logisim project ArchiProc.circ as structural Verilog: 6 circuits, main circuit main
module main (
);

  wire clk_out, instdecoder_1_isjmp, instdecoder_1_isload, instdecoder_1_regwrite, RESET_out;
  wire [1:0] jmpcontroller_1_nextpcselect;
  wire [2:0] instdecoder_1_ctrual;
  wire [3:0] regselector_1_rd, regselector_1_rs, regselector_1_rt_2, ual_1_flags;
  wire [7:0] adder_1_out, adder_2_out, bit_extender_1_out, multiplexer_1_out, multiplexer_2_out, PC_q,
       regbank_1_rs_2, regbank_1_rt_2, ual_1_res;
  wire [15:0] ram_1_data;

  Button RESET (.out(RESET_out));
  Counter #(.ongoal("stay")) PC (
    .D(multiplexer_2_out), .Q(PC_q), .clk(clk_out), .clr(RESET_out));  // open: load, count, carry
  Clock clk (.out(clk_out));
  RAM #(.dataWidth(16)) ram_1 (.addr(PC_q), .data(ram_1_data), .clk(clk_out));  // open: sel, ld, clr
  Adder adder_1 (.a(PC_q), .b(8'h1), .out(adder_1_out));  // open: cin, cout
  instDecoder instdecoder_1 (
    .opcode(ram_1_data[15:12]), .isLoad(instdecoder_1_isload), .ctrUAL(instdecoder_1_ctrual),
    .isJMP(instdecoder_1_isjmp), .regWrite(instdecoder_1_regwrite));
  assign bit_extender_1_out = {{4{ram_1_data[3]}}, ram_1_data[3:0]};  // Bit_Extender bit_extender_1
  regSelector regselector_1 (
    .isJMP(instdecoder_1_isjmp), .rd_rs(ram_1_data[11:8]), .rs_rt(ram_1_data[7:4]), .rt(ram_1_data[3:0]),
    .rd(regselector_1_rd), .rs(regselector_1_rs), .rt_2(regselector_1_rt_2));
  regBank regbank_1 (
    .RESET(RESET_out), .regWrite(instdecoder_1_regwrite), .clk(clk_out), .valIn(multiplexer_1_out),
    .Rs_2(regbank_1_rs_2), .Rt_2(regbank_1_rt_2), .Rd(regselector_1_rd), .Rs(regselector_1_rs),
    .Rt(regselector_1_rt_2));
  Multiplexer #(.width(8), .enable("false")) multiplexer_1 (
    .in0(ual_1_res), .in1(ram_1_data[7:0]), .out(multiplexer_1_out), .sel(instdecoder_1_isload));
  Adder adder_2 (.a(adder_1_out), .b(bit_extender_1_out), .out(adder_2_out));  // open: cin, cout
  UAL ual_1 (
    .Rs(regbank_1_rs_2), .Rt(regbank_1_rt_2), .res(ual_1_res), .flags(ual_1_flags),
    .ctrUAL(instdecoder_1_ctrual));
  Multiplexer #(.select(2), .width(8), .enable("false")) multiplexer_2 (
    .in0(adder_1_out), .in1({8{1'b1}}), .in2(adder_2_out), .out(multiplexer_2_out),
    .sel(jmpcontroller_1_nextpcselect));  // open: in3
  jmpController jmpcontroller_1 (
    .flags(ual_1_flags), .nextPCselect(jmpcontroller_1_nextpcselect), .opcode(ram_1_data[15:12]));

  // Notes on the sheet:
  //   "instruction suivante"
  //   "HALT"
  //   "saut"
endmodule

module UAL (
  input  [7:0] Rs,
  input  [2:0] ctrUAL,
  input  [7:0] Rt,
  output [3:0] flags,
  output [7:0] res
);

  wire adder_1_cout, OF, or_3_out, subtractor_1_bout;
  wire [2:0] bitselector_1_out;
  wire [7:0] adder_1_out, and_1_out, not_1_out, or_1_out, shifter_1_out, shifter_2_out, subtractor_1_out;

  BitSelector #(.group(3)) bitselector_1 (.in(Rt), .out(bitselector_1_out), .sel(2'b00));
  Adder adder_1 (.a(Rs), .b(Rt), .out(adder_1_out), .cout(adder_1_cout));  // open: cin
  Subtractor subtractor_1 (.a(Rs), .b(Rt), .out(subtractor_1_out), .bout(subtractor_1_bout));  // open: bin
  assign or_1_out = Rs | Rt;  // OR_Gate or_1, 8 bits wide
  assign and_1_out = Rs & Rt;  // AND_Gate and_1, 8 bits wide
  assign not_1_out = ~Rs;  // NOT_Gate not_1, 8 bits wide
  Shifter shifter_1 (.in(Rs), .\dist (bitselector_1_out), .out(shifter_1_out));
  Shifter #(.shift("lr")) shifter_2 (.in(Rs), .\dist (bitselector_1_out), .out(shifter_2_out));
  or or_2 (OF, Rs[7], Rt[7]);
  Multiplexer #(.select(3), .enable("false")) multiplexer_1 (
    .in0(adder_1_cout), .in1(subtractor_1_bout), .in2(1'b0), .in3(1'b0), .in4(1'b0), .in5(1'b0), .in6(1'b0),
    .out(flags[3]), .sel(ctrUAL));  // open: in7
  or or_3 (or_3_out, res[0], res[1], res[2], res[3], res[4], res[5], res[6], flags[1]);
  not not_2 (flags[2], or_3_out);
  Multiplexer #(.select(3), .width(8), .enable("false")) multiplexer_2 (
    .in0(adder_1_out), .in1(subtractor_1_out), .in2(or_1_out), .in3(and_1_out), .in4(not_1_out),
    .in5(shifter_1_out), .in6(shifter_2_out), .out({flags[1], res[6:0]}), .sel(ctrUAL));  // open: in7
  xor xor_1 (flags[0], flags[1], OF);

  assign res[7] = flags[1];

  // Other names for the same wires on the sheet: CF[2:0] = ctrUAL; SF[7:0] = {flags[1], res[6:0]};
  //   ZF[7:0] = {flags[1], res[6:0]}
endmodule

module instDecoder (
  input  [3:0] opcode,
  output isJMP,
  output regWrite,
  output isLoad,
  output [2:0] ctrUAL
);

  wire and_1_out, and_2_out, and_3_out;

  and and_1 (and_1_out, opcode[3], opcode[2]);
  or or_1 (isJMP, and_1_out, and_3_out, and_2_out);
  and and_2 (and_2_out, opcode[3], opcode[1]);
  and and_3 (and_3_out, opcode[3], ~opcode[1], opcode[0]);  // AND_Gate
  not not_1 (regWrite, opcode[3]);
  and and_4 (isLoad, ~opcode[3], opcode[2], opcode[1], opcode[0]);  // AND_Gate
  Multiplexer #(.width(3), .enable("false")) multiplexer_1 (
    .in0(opcode[2:0]), .in1(3'b001), .out(ctrUAL), .sel(opcode[3]));
endmodule

module jmpController (
  input  [3:0] flags,
  input  [3:0] opcode,
  output [1:0] nextPCselect
);

  wire and_1_out, and_2_out, and_3_out, and_4_out, and_5_out, and_6_out, b_out, beq_out, bge, bge_out, bgt,
       bgt_out, ble, ble_out, blt, blt_out, bne_out, xnor_1_out, xnor_2_out, xor_1_out, xor_2_out;

  xnor xnor_1 (xnor_1_out, flags[0], flags[1]);
  xor xor_1 (xor_1_out, flags[0], flags[1]);
  xnor xnor_2 (xnor_2_out, flags[0], flags[1]);
  xor xor_2 (xor_2_out, flags[0], flags[1]);
  or or_1 (bge, xnor_1_out, flags[2]);
  or or_2 (ble, xor_1_out, flags[2]);
  or or_3 (bgt, xnor_2_out, flags[2]);
  or or_4 (blt, xor_2_out, flags[2]);
  or or_5 (nextPCselect[1], and_6_out, and_5_out, and_4_out, and_3_out, and_2_out, and_1_out, b_out);
  and and_1 (and_1_out, beq_out, flags[1]);
  and and_2 (and_2_out, bne_out, ~flags[1]);  // AND_Gate
  and and_3 (and_3_out, bge_out, bge);
  and and_4 (and_4_out, ble_out, ble);
  and and_5 (and_5_out, bgt_out, bgt);
  and and_6 (and_6_out, blt_out, blt);
  and b (b_out, opcode[0], ~opcode[1], ~opcode[2], opcode[3]);  // AND_Gate
  and beq (beq_out, ~opcode[0], opcode[1], ~opcode[2], opcode[3]);  // AND_Gate
  and bne (bne_out, opcode[0], opcode[1], ~opcode[2], opcode[3]);  // AND_Gate
  and u_bge (bge_out, ~opcode[0], ~opcode[1], opcode[2], opcode[3]);  // AND_Gate
  and u_ble (ble_out, opcode[0], ~opcode[1], opcode[2], opcode[3]);  // AND_Gate
  and u_bgt (bgt_out, opcode[0], opcode[1], opcode[2], opcode[3]);
  and u_blt (blt_out, opcode[0], ~opcode[1], ~opcode[2], opcode[3]);  // AND_Gate
  and HALT (nextPCselect[0], ~opcode[0], ~opcode[1], ~opcode[2], opcode[3]);  // AND_Gate

  // Other names for the same wires on the sheet: beq = flags[1]; bne = flags[1]

  // Notes on the sheet:
  //   On code 00 : "instruction suivante"
  //   01 : "HALT"
  //   10 : "saut"
endmodule

module regBank (
  input  [3:0] Rd,
  input  [3:0] Rs,
  input  [3:0] Rt,
  input  [7:0] valIn,
  input  RESET,
  input  clk,
  input  regWrite,
  output [7:0] Rs_2,
  output [7:0] Rt_2
);

  wire demultiplexer_1_out0, demultiplexer_1_out1, demultiplexer_1_out2, demultiplexer_1_out3,
       demultiplexer_1_out4, demultiplexer_1_out5, demultiplexer_1_out6, demultiplexer_1_out7,
       demultiplexer_1_out8, demultiplexer_1_out9, demultiplexer_1_out10, demultiplexer_1_out11,
       demultiplexer_1_out12, demultiplexer_1_out13, demultiplexer_1_out14, demultiplexer_1_out15;
  wire [7:0] register_1_q, register_2_q, register_3_q, register_4_q, register_5_q, register_6_q,
       register_7_q, register_8_q, register_9_q, register_10_q, register_11_q, register_12_q, register_13_q,
       register_14_q, register_15_q, register_16_q;

  Demultiplexer #(.select(4), .enable("false")) demultiplexer_1 (
    .out0(demultiplexer_1_out0), .out1(demultiplexer_1_out1), .out2(demultiplexer_1_out2),
    .out3(demultiplexer_1_out3), .out4(demultiplexer_1_out4), .out5(demultiplexer_1_out5),
    .out6(demultiplexer_1_out6), .out7(demultiplexer_1_out7), .out8(demultiplexer_1_out8),
    .out9(demultiplexer_1_out9), .out10(demultiplexer_1_out10), .out11(demultiplexer_1_out11),
    .out12(demultiplexer_1_out12), .out13(demultiplexer_1_out13), .out14(demultiplexer_1_out14),
    .out15(demultiplexer_1_out15), .in(regWrite), .sel(Rd));
  Register register_1 (.D(valIn), .en(demultiplexer_1_out0), .Q(register_1_q), .clk(clk), .clr(RESET));
  Register register_2 (.D(valIn), .en(demultiplexer_1_out1), .Q(register_2_q), .clk(clk), .clr(RESET));
  Register register_3 (.D(valIn), .en(demultiplexer_1_out2), .Q(register_3_q), .clk(clk), .clr(RESET));
  Register register_4 (.D(valIn), .en(demultiplexer_1_out3), .Q(register_4_q), .clk(clk), .clr(RESET));
  Register register_5 (.D(valIn), .en(demultiplexer_1_out4), .Q(register_5_q), .clk(clk), .clr(RESET));
  Register register_6 (.D(valIn), .en(demultiplexer_1_out5), .Q(register_6_q), .clk(clk), .clr(RESET));
  Register register_7 (.D(valIn), .en(demultiplexer_1_out6), .Q(register_7_q), .clk(clk), .clr(RESET));
  Register register_8 (.D(valIn), .en(demultiplexer_1_out7), .Q(register_8_q), .clk(clk), .clr(RESET));
  Register register_9 (.D(valIn), .en(demultiplexer_1_out8), .Q(register_9_q), .clk(clk), .clr(RESET));
  Register register_10 (.D(valIn), .en(demultiplexer_1_out9), .Q(register_10_q), .clk(clk), .clr(RESET));
  Register register_11 (.D(valIn), .en(demultiplexer_1_out10), .Q(register_11_q), .clk(clk), .clr(RESET));
  Register register_12 (.D(valIn), .en(demultiplexer_1_out11), .Q(register_12_q), .clk(clk), .clr(RESET));
  Register register_13 (.D(valIn), .en(demultiplexer_1_out12), .Q(register_13_q), .clk(clk), .clr(RESET));
  Register register_14 (.D(valIn), .en(demultiplexer_1_out13), .Q(register_14_q), .clk(clk), .clr(RESET));
  Register register_15 (.D(valIn), .en(demultiplexer_1_out14), .Q(register_15_q), .clk(clk), .clr(RESET));
  Register register_16 (.D(valIn), .en(demultiplexer_1_out15), .Q(register_16_q), .clk(clk), .clr(RESET));
  Multiplexer #(.select(4), .width(8), .enable("false")) multiplexer_1 (
    .in0(register_1_q), .in1(register_2_q), .in2(register_3_q), .in3(register_4_q), .in4(register_5_q),
    .in5(register_6_q), .in6(register_7_q), .in7(register_8_q), .in8(register_9_q), .in9(register_10_q),
    .in10(register_11_q), .in11(register_12_q), .in12(register_13_q), .in13(register_14_q),
    .in14(register_15_q), .in15(register_16_q), .out(Rt_2), .sel(Rt));
  Multiplexer #(.select(4), .width(8), .enable("false")) multiplexer_2 (
    .in0(register_1_q), .in1(register_2_q), .in2(register_3_q), .in3(register_4_q), .in4(register_5_q),
    .in5(register_6_q), .in6(register_7_q), .in7(register_8_q), .in8(register_9_q), .in9(register_10_q),
    .in10(register_11_q), .in11(register_12_q), .in12(register_13_q), .in13(register_14_q),
    .in14(register_15_q), .in15(register_16_q), .out(Rs_2), .sel(Rs));

  // Other names for the same wires on the sheet: vallin[7:0] = valIn
endmodule

module regSelector (
  input  [3:0] rd_rs,
  input  [3:0] rs_rt,
  input  [3:0] rt,
  input  isJMP,
  output [3:0] rd,
  output [3:0] rs,
  output [3:0] rt_2
);

  wire [3:0] demultiplexer_1_out0, demultiplexer_1_out0_2, demultiplexer_1_out0_3;
  wire [11:0] demultiplexer_1_out1;

  Multiplexer #(.width(4), .enable("false")) multiplexer_1 (
    .in0(demultiplexer_1_out0_3), .out(rd), .sel(isJMP));  // open: in1
  Multiplexer #(.width(4), .enable("false")) multiplexer_2 (
    .in0(demultiplexer_1_out0_2), .in1(demultiplexer_1_out1[11:8]), .out(rs), .sel(isJMP));
  Multiplexer #(.width(4), .enable("false")) multiplexer_3 (
    .in0(demultiplexer_1_out0), .in1(demultiplexer_1_out1[7:4]), .out(rt_2), .sel(isJMP));
  Demultiplexer #(.width(12), .enable("false")) demultiplexer_1 (
    .out0({demultiplexer_1_out0_3, demultiplexer_1_out0_2, demultiplexer_1_out0}),
    .out1(demultiplexer_1_out1), .in({rd_rs, rs_rt, rt}), .sel(isJMP));
endmodule
